# Fritzing sketch schema2 (saved by Fritzing 0.9.3b)
breadboards: 1

parts:
  Raspberry_Pi1 = Raspberry Pi B+  # not connected
  Part1 = Arduino Mega 2560 (Rev3)
  M1 = bb-usb-cable [package=THT]  # not connected
  U1 = LCD-16X2 [package=lcd-16x2_noholes]
  U4 = 74HC4052 [package=dil16]
  U5 = POT [package=alps_pot]
  Power_plug1 = USB-C plug  # not connected
  VCC1 = Battery block 9V
  J1 = Basic Servo
  R1 = Resistor [tolerance=±5% resistance=220 package="0402 [SMD]"]

nets:
  N1: Part1.D12_PWM, U1.RS
  N2: Part1.D11_PWM, U1.E
  N3: Part1.D10_PWM, U4.Y0, U4.X2
  5V: Part1.5V, U1.VDD, U1.A, U4.VCC, U5.E, R1.Pin_0
  GND: Part1.GND, U1.VSS, U1.R_W, U1.K, U5.A, VCC1.-
  N4: Part1.D0_RX0, U4.X1
  N5: Part1.D1_TX0, U4.X
  N6: Part1.D2_PWM, U1.DB7
  N7: Part1.D3_PWM, U1.DB6
  N8: Part1.D4_PWM, U1.DB5
  N9: Part1.D5_PWM, U1.DB4
  N10: U1.VO, U5.S
  N11: U4.Y2, U4.Y, J1.pulse, R1.Pin_1
  GND_2: U4.GND, J1.gnd

custom parts:
  bb-usb-cable: Breadboard only, no connectors USB cable for the Raspberry PIs.
  USB-C plug: power plug
