# Fritzing sketch schema3 (saved by Fritzing 0.9.3b)
breadboards: 1

parts:
  U4 = 74HC4052 [package=dil16]
  J1 = Basic Servo
  R1 = Resistor [tolerance=±5% resistance=220 package="0402 [SMD]"]
  Part2 = Arduino Uno (Rev3)
  VCC1 = Battery block 9V
  U5 = POT [package=pot_mammoth]

nets:
  N1: U4.Y0, U4.X2, Part2.D10_PWM/SS
  N2: U4.Y2, U4.Y, J1.pulse, R1.Pin_1
  GND: U4.GND, J1.gnd
  N3: U4.X, Part2.D1/TX
  N4: U4.X1, Part2.D0/RX
  VCC: U4.VCC, R1.Pin_0, Part2.5V, U5.E
  N5: Part2.A2, U5.A
  N6: Part2.GND, VCC1.-, U5.S
